# Fritzing sketch Arcobaleno-variante (saved by Fritzing 0.9.3b)
breadboards: 1

parts:
  Componente1 = Arduino Uno (Rev3)
  LED1 = RGB LED (com. cathode, rgb) [package="5 mm [THT]"]
  R1 = Resistor [tolerance=±5% resistance=220 package=THT]
  R2 = Resistor [tolerance=±5% resistance=220 package=THT]
  R3 = Resistor [tolerance=±5% resistance=220 package=THT]

nets:
  N1: Componente1.D9_PWM, R1.Pin_0
  N2: LED1.red_anode, R1.Pin_1
  N3: LED1.green_anode, R2.Pin_1
  N4: LED1.blue_anode, R3.Pin_1
